// Logisim project arq_TP.circ as structural Verilog: 47 circuits, main circuit Pantalla_Juego
module Pantalla_Juego (
);

  wire ABJ, and_1_out, and_2_out, and_3_out, and_4_out, and_5_out, ARR, c44, CLK, comparator_1_eq,
       comparator_2_eq, comparator_3_eq, comparator_4_eq, comparator_5_eq, cx2, DER, E, Escritura_fin,
       Escritura_pozo, FIN, GEN, IZQ, J1G, J2G, J3G, J4G, l00, l01, l02, l03, l04, l05, l10, l11, l12, l13,
       l14, l15, l20, l21, l22, l23, l24, l25, l30, l31, l32, l33, l34, l35, l40, l41, l42, l43, l44, l45,
       l50, l51, l52, l53, l54, l55, not_1_out, not_2_out, not_3_out, not_4_out, not_5_out, not_6_out,
       not_7_out, not_8_out, not_9_out, or_1_out, or_2_out, or_3_out, or_4_out, or_5_out, or_6_out, or_7_out,
       or_8_out, or_9_out, or_10_out, POZO, s, SP;
  wire [2:0] counter_1_q, multiplexer_1_out, multiplexer_3_out, multiplexer_6_out, multiplexer_8_out, pos_mem;
  wire [3:0] cent, COL, dec, FILA, jug, P, prox_part, un;
  wire [7:0] cbin, chex, multiplexer_2_out, multiplexer_4_out, multiplexer_5_out, multiplexer_7_out, P1, P2,
       P3, P4;

  Comparator #(.width(4)) comparator_1 (.a(jug), .b(4'b0001), .eq(comparator_1_eq));  // open: gt, lt
  a9_Contador a9_contador_1 (.POZO(POZO), .FIN(FIN), .cx2(cx2));
  _7_Segment_Display u_7_segment_display_1 (.g(s));  // open: f, a, b, e, d, c, dp
  Comparator #(.width(4)) comparator_2 (.a(jug), .b(4'b0011), .eq(comparator_2_eq));  // open: gt, lt
  D_Flip_Flop d_ff_1 (.D(POZO), .clk(POZO), .Q(Escritura_pozo), .reset(c44));  // open: Qn, preset
  _7_Segment_Display u_7_segment_display_2 ();  // open: g, f, a, b, e, d, c, dp
  // BCD_to_7_Segment_decoder bcd_to_7_segment_decoder_1: pin names not known; wires that end beside it: cent
  _7_Segment_Display u_7_segment_display_3 ();  // open: g, f, a, b, e, d, c, dp
  // BCD_to_7_Segment_decoder bcd_to_7_segment_decoder_2: pin names not known; wires that end beside it: jug
  and and_1 (and_1_out, comparator_1_eq, cx2);
  and and_2 (and_2_out, comparator_2_eq, cx2);
  _7_Segment_Display u_7_segment_display_4 ();  // open: g, f, a, b, e, d, c, dp
  // BCD_to_7_Segment_decoder bcd_to_7_segment_decoder_3: pin names not known; wires that end beside it: dec
  _7_Segment_Display u_7_segment_display_5 ();  // open: g, f, a, b, e, d, c, dp
  // BCD_to_7_Segment_decoder bcd_to_7_segment_decoder_4: pin names not known; wires that end beside it: FILA
  _7_Segment_Display u_7_segment_display_6 ();  // open: g, f, a, b, e, d, c, dp
  // BCD_to_7_Segment_decoder bcd_to_7_segment_decoder_5: pin names not known; wires that end beside it: prox_part
  Multiplexer #(.width(3)) multiplexer_1 (.in0(P[2:0]), .in1(pos_mem), .out(multiplexer_1_out), .sel(or_1_out));
  or or_1 (or_1_out, Escritura_pozo, Escritura_fin);
  not not_1 (not_1_out, SP);
  Multiplexer #(.width(8)) multiplexer_2 (.in0(chex), .in1(8'h1), .out(multiplexer_2_out), .sel(Escritura_pozo));
  Multiplexer #(.width(3)) multiplexer_3 (.in0(P[2:0]), .in1(pos_mem), .out(multiplexer_3_out), .sel(or_2_out));
  or or_2 (or_2_out, Escritura_pozo, Escritura_fin);
  not not_2 (not_2_out, SP);
  Multiplexer #(.width(8)) multiplexer_4 (.in0(chex), .in1(8'h1), .out(multiplexer_4_out), .sel(Escritura_pozo));
  _7_Segment_Display u_7_segment_display_7 ();  // open: g, f, a, b, e, d, c, dp
  // BCD_to_7_Segment_decoder bcd_to_7_segment_decoder_6: pin names not known; wires that end beside it: un
  _7_Segment_Display u_7_segment_display_8 ();  // open: g, f, a, b, e, d, c, dp
  // BCD_to_7_Segment_decoder bcd_to_7_segment_decoder_7: pin names not known; wires that end beside it: COL
  RAM #(.addrWidth(3)) ram_1 (
    .addr(multiplexer_1_out), .we(or_1_out), .oe(not_1_out), .clk(not_3_out), .din(multiplexer_2_out),
    .dout(P1));
  not not_3 (not_3_out, or_3_out);
  or or_3 (or_3_out, SP, and_1_out);
  RAM #(.addrWidth(3)) ram_2 (
    .addr(multiplexer_3_out), .we(or_2_out), .oe(not_2_out), .clk(not_4_out), .din(multiplexer_4_out),
    .dout(P3));
  not not_4 (not_4_out, or_4_out);
  or or_4 (or_4_out, SP, and_2_out);
  Clock clock_1 (.out(CLK));
  LED led_1 (.in(l00));
  LED led_2 (.in(l10));
  LED led_3 (.in(l20));
  LED led_4 (.in(l30));
  LED led_5 (.in(l40));
  LED led_6 (.in(l50));
  or or_5 (or_5_out, POZO, FIN);
  LED led_7 (.in(l01));
  LED led_8 (.in(l11));
  LED led_9 (.in(l21));
  LED led_10 (.in(l31));
  LED led_11 (.in(l41));
  LED led_12 (.in(l51));
  Counter #(.max('h5), .width(3)) counter_1 (
    .clr(and_3_out), .clk(or_5_out), .Q(counter_1_q));  // open: load, up, count, D, carry
  a5_Tablero a5_tablero_1 (
    .GEN(GEN), .ARR(ARR), .IZQ(IZQ), .DER(DER), .ABJ(ABJ), .COL(COL), .FILA(FILA), .chex(chex), .cbin(cbin),
    .POZO(POZO), .FIN(FIN), .l00(l00), .l01(l01), .l02(l02), .l03(l03), .l04(l04), .l05(l05), .l10(l10),
    .l11(l11), .l12(l12), .l13(l13), .l14(l14), .l15(l15), .l20(l20), .l21(l21), .l22(l22), .l23(l23),
    .l24(l24), .l25(l25), .l30(l30), .l31(l31), .l32(l32), .l33(l33), .l34(l34), .l35(l35), .l40(l40),
    .l41(l41), .l42(l42), .l43(l43), .l44(l44), .l45(l45), .l50(l50), .l51(l51), .l52(l52), .l53(l53),
    .l54(l54), .l55(l55));
  LED led_13 (.in(l02));
  LED led_14 (.in(l12));
  LED led_15 (.in(l22));
  LED led_16 (.in(l32));
  LED led_17 (.in(l42));
  LED led_18 (.in(l52));
  not not_5 (not_5_out, or_6_out);
  and and_3 (and_3_out, not_5_out, comparator_3_eq);
  or or_6 (or_6_out, Escritura_fin, Escritura_pozo);
  LED led_19 (.in(l03));
  LED led_20 (.in(l13));
  LED led_21 (.in(l23));
  LED led_22 (.in(l33));
  LED led_23 (.in(l43));
  LED led_24 (.in(l53));
  Comparator #(.mode("unsigned"), .width(3)) comparator_3 (
    .a(counter_1_q), .b(3'b100), .eq(comparator_3_eq));  // open: gt, lt
  LED led_25 (.in(l04));
  LED led_26 (.in(l14));
  LED led_27 (.in(l24));
  LED led_28 (.in(l34));
  LED led_29 (.in(l44));
  LED led_30 (.in(l54));
  LED led_31 (.in(l05));
  LED led_32 (.in(l15));
  LED led_33 (.in(l25));
  LED led_34 (.in(l35));
  LED led_35 (.in(l45));
  LED led_36 (.in(l55));
  Counter #(.max('h7), .ongoal("stay"), .width(3)) counter_2 (
    .clk(and_3_out), .Q(pos_mem));  // open: clr, load, up, count, D, carry
  a6_Jugador_Jugando a6_jugador_jugando_1 (
    .POZO(POZO), .FIN(FIN), .c44(c44), .PROX_PARTIDA_EN(prox_part), .JUGADOR(jug));
  a7_Puntaje_Final a7_puntaje_final_1 (.POZO(POZO), .cbin(cbin), .signo(s), .u(un), .c(cent), .d(dec));
  a8_Seleccionar_Partida a8_seleccionar_partida_1 (.SP(SP), .P(P));
  a10_Comprobar_Ganador_Historial a10_comprobar_ganador_historial_1 (
    .P4(P4), .P3(P3), .P2(P2), .P1(P1), .JUG_1_GANADOR(J1G), .JUG_2_GANADOR(J2G), .JUG_3_GANADOR(J3G),
    .JUG_4_GANADOR(J4G), .EMPATE(E));
  LED J1 (.in(J1G));
  Button button_1 (.out(IZQ));
  Comparator #(.width(4)) comparator_4 (.a(jug), .b(4'b0010), .eq(comparator_4_eq));  // open: gt, lt
  Comparator #(.width(4)) comparator_5 (.a(jug), .b(4'b0100), .eq(comparator_5_eq));  // open: gt, lt
  Button GENERADOR (.out(GEN));
  _7_Segment_Display u_7_segment_display_9 ();  // open: g, f, a, b, e, d, c, dp
  // BCD_to_7_Segment_decoder bcd_to_7_segment_decoder_8: pin names not known; wires that end beside it: P
  Button button_2 (.out(SP));
  LED J2 (.in(J2G));
  LED u_E (.in(E));
  LED J3 (.in(J3G));
  Button button_3 (.out(ARR));
  Button button_4 (.out(ABJ));
  and and_4 (and_4_out, comparator_5_eq, cx2);
  LED J4 (.in(J4G));
  Button button_5 (.out(DER));
  or or_7 (or_7_out, Escritura_pozo, Escritura_fin);
  and and_5 (and_5_out, comparator_4_eq, cx2);
  or or_8 (or_8_out, Escritura_pozo, Escritura_fin);
  Multiplexer #(.width(8)) multiplexer_5 (.in0(chex), .in1(8'h1), .out(multiplexer_5_out), .sel(Escritura_pozo));
  D_Flip_Flop d_ff_2 (.D(FIN), .clk(FIN), .Q(Escritura_fin), .reset(c44));  // open: Qn, preset
  Multiplexer #(.width(3)) multiplexer_6 (.in0(P[2:0]), .in1(pos_mem), .out(multiplexer_6_out), .sel(or_7_out));
  not not_6 (not_6_out, SP);
  or or_9 (or_9_out, SP, and_5_out);
  Multiplexer #(.width(8)) multiplexer_7 (.in0(chex), .in1(8'h1), .out(multiplexer_7_out), .sel(Escritura_pozo));
  Multiplexer #(.width(3)) multiplexer_8 (.in0(P[2:0]), .in1(pos_mem), .out(multiplexer_8_out), .sel(or_8_out));
  not not_7 (not_7_out, SP);
  or or_10 (or_10_out, SP, and_4_out);
  RAM #(.addrWidth(3)) ram_3 (
    .addr(multiplexer_6_out), .we(or_7_out), .oe(not_6_out), .clk(not_8_out), .din(multiplexer_7_out),
    .dout(P2));
  not not_8 (not_8_out, or_9_out);
  RAM #(.addrWidth(3)) ram_4 (
    .addr(multiplexer_8_out), .we(or_8_out), .oe(not_7_out), .clk(not_9_out), .din(multiplexer_5_out),
    .dout(P4));
  not not_9 (not_9_out, or_10_out);

  // Notes on the sheet:
  //   JUGADOR
  //   PUNTOS
  //   PRÓXIMA PARTIDA EN
  //   POSICIÓN
  //   (0,0)
  //   (1,0)
  //   (2,0)
  //   (3,0)
  //   (4,0)
  //   (5,0)
  //   HISTORIAL JUGADOR 1
  //   HISTORIAL JUGADOR 3
  //   (0,1)
  //   (1,1)
  //   (2,1)
  //   (3,1)
  //   (4,1)
  //   (5,1)
  //   (0,2)
  //   (1,2)
  //   (2,2)
  //   (3,2)
  //   (4,2)
  //   (5,2)
  //   (0,3)
  //   (1,3)
  //   (2,3)
  //   (3,3)
  //   (4,3)
  //   (5,3)
  //   ========================================= MEMORIAS ========================================
  //   (0,4)
  //   (1,4)
  //   (2,4)
  //   (3,4)
  //   (4,4)
  //   (5,4)
  //   (0,5)
  //   (1,5)
  //   (2,5)
  //   (3,5)
  //   (4,5)
  //   (5,5)
  //   PARTIDA
  //   CONTROLES
  //   HISTORIAL JUGADOR 2
  //   HISTORIAL JUGADOR 4
endmodule

module a1_Estado_Matriz (
  input  in_1,
  input  in_2,
  output GOMA,
  output POZO,
  output HIELO,
  output PREMIO
);

  wire not_1_out, not_2_out, not_3_out, not_4_out;

  not not_1 (not_1_out, in_1);
  and and_1 (GOMA, not_1_out, not_2_out);
  not not_2 (not_2_out, in_2);
  not not_3 (not_3_out, in_1);
  and and_2 (POZO, not_3_out, in_2);
  and and_3 (HIELO, in_1, not_4_out);
  not not_4 (not_4_out, in_2);
  and and_4 (PREMIO, in_2, in_1);
endmodule

module a2_Estado_Actual (
  input  POS,
  input  PO,
  input  HIEL,
  input  PRE,
  output POZO,
  output HIELO,
  output PREMIO
);

  and and_1 (POZO, PO, POS);
  and and_2 (HIELO, HIEL, POS);
  and and_3 (PREMIO, PRE, POS);
endmodule

module a3_Posicion (
  input  [3:0] FILA,
  input  [3:0] COL,
  output s0_0,
  output s0_1,
  output s0_2,
  output s0_3,
  output s0_4,
  output s0_5,
  output s1_0,
  output s1_1,
  output s1_2,
  output s1_3,
  output s1_4,
  output s1_5,
  output s2_0,
  output s2_1,
  output s2_2,
  output s2_3,
  output s2_4,
  output s2_5,
  output s3_0,
  output s3_1,
  output s3_2,
  output s3_3,
  output s3_4,
  output s3_5,
  output s4_0,
  output s4_1,
  output s4_2,
  output s4_3,
  output s4_4,
  output s4_5,
  output s5_0,
  output s5_1,
  output s5_2,
  output s5_3,
  output s5_4,
  output s5_5
);

  wire not_1_out, not_2_out, not_3_out, not_4_out, not_5_out, not_6_out, not_7_out, not_8_out;

  not not_1 (not_1_out, FILA[3]);
  not not_2 (not_2_out, FILA[2]);
  not not_3 (not_3_out, FILA[1]);
  not not_4 (not_4_out, FILA[0]);
  not not_5 (not_5_out, COL[3]);
  not not_6 (not_6_out, COL[2]);
  not not_7 (not_7_out, COL[1]);
  not not_8 (not_8_out, COL[0]);
  and and_1 (s0_0, not_8_out, not_7_out, not_6_out, not_5_out, not_4_out, not_3_out, not_2_out, not_1_out);
  and and_2 (s0_1, COL[0], not_7_out, not_6_out, not_5_out, not_4_out, not_3_out, not_2_out, not_1_out);
  and and_3 (s0_2, COL[1], not_8_out, not_6_out, not_5_out, not_4_out, not_3_out, not_2_out, not_1_out);
  and and_4 (s0_3, COL[1], COL[0], not_6_out, not_5_out, not_4_out, not_3_out, not_2_out, not_1_out);
  and and_5 (s0_4, COL[2], not_8_out, not_7_out, not_5_out, not_4_out, not_3_out, not_2_out, not_1_out);
  and and_6 (s0_5, COL[2], COL[0], not_7_out, not_5_out, not_4_out, not_3_out, not_2_out, not_1_out);
  and and_7 (s1_0, FILA[0], not_8_out, not_7_out, not_6_out, not_5_out, not_3_out, not_2_out, not_1_out);
  and and_8 (s1_1, FILA[0], COL[0], not_7_out, not_6_out, not_5_out, not_3_out, not_2_out, not_1_out);
  and and_9 (s1_2, FILA[0], COL[1], not_8_out, not_6_out, not_5_out, not_3_out, not_2_out, not_1_out);
  and and_10 (s1_3, FILA[0], COL[1], COL[0], not_6_out, not_5_out, not_3_out, not_2_out, not_1_out);
  and and_11 (s1_4, FILA[0], COL[2], not_8_out, not_7_out, not_5_out, not_3_out, not_2_out, not_1_out);
  and and_12 (s1_5, FILA[0], COL[2], COL[0], not_7_out, not_5_out, not_3_out, not_2_out, not_1_out);
  and and_13 (s2_0, FILA[1], not_8_out, not_7_out, not_6_out, not_5_out, not_4_out, not_2_out, not_1_out);
  and and_14 (s2_1, FILA[1], COL[0], not_7_out, not_6_out, not_5_out, not_4_out, not_2_out, not_1_out);
  and and_15 (s2_2, FILA[1], COL[1], not_8_out, not_6_out, not_5_out, not_4_out, not_2_out, not_1_out);
  and and_16 (s2_3, FILA[1], COL[1], COL[0], not_6_out, not_5_out, not_4_out, not_2_out, not_1_out);
  and and_17 (s2_4, FILA[1], COL[2], not_8_out, not_7_out, not_5_out, not_4_out, not_2_out, not_1_out);
  and and_18 (s2_5, FILA[1], COL[2], COL[0], not_7_out, not_5_out, not_4_out, not_2_out, not_1_out);
  and and_19 (s3_0, FILA[1], FILA[0], not_8_out, not_7_out, not_6_out, not_5_out, not_2_out, not_1_out);
  and and_20 (s3_1, FILA[1], FILA[0], COL[0], not_7_out, not_6_out, not_5_out, not_2_out, not_1_out);
  and and_21 (s3_2, FILA[1], FILA[0], COL[1], not_8_out, not_6_out, not_5_out, not_2_out, not_1_out);
  and and_22 (s3_3, FILA[1], FILA[0], COL[1], COL[0], not_6_out, not_5_out, not_2_out, not_1_out);
  and and_23 (s3_4, FILA[1], FILA[0], COL[2], not_8_out, not_7_out, not_5_out, not_2_out, not_1_out);
  and and_24 (s3_5, FILA[1], FILA[0], COL[2], COL[0], not_7_out, not_5_out, not_2_out, not_1_out);
  and and_25 (s4_0, FILA[2], not_8_out, not_7_out, not_6_out, not_5_out, not_4_out, not_3_out, not_1_out);
  and and_26 (s4_1, FILA[2], COL[0], not_7_out, not_6_out, not_5_out, not_4_out, not_3_out, not_1_out);
  and and_27 (s4_2, FILA[2], COL[1], not_8_out, not_6_out, not_5_out, not_4_out, not_3_out, not_1_out);
  and and_28 (s4_3, FILA[2], COL[1], COL[0], not_6_out, not_5_out, not_4_out, not_3_out, not_1_out);
  and and_29 (s4_4, FILA[2], COL[2], not_8_out, not_7_out, not_5_out, not_4_out, not_3_out, not_1_out);
  and and_30 (s4_5, FILA[2], COL[2], COL[0], not_7_out, not_5_out, not_4_out, not_3_out, not_1_out);
  and and_31 (s5_0, FILA[2], FILA[0], not_8_out, not_7_out, not_6_out, not_5_out, not_3_out, not_1_out);
  and and_32 (s5_1, FILA[2], FILA[0], COL[0], not_7_out, not_6_out, not_5_out, not_3_out, not_1_out);
  and and_33 (s5_2, FILA[2], FILA[0], COL[1], not_8_out, not_6_out, not_5_out, not_3_out, not_1_out);
  and and_34 (s5_3, FILA[2], FILA[0], COL[1], COL[0], not_6_out, not_5_out, not_3_out, not_1_out);
  and and_35 (s5_4, FILA[2], FILA[0], COL[2], not_8_out, not_7_out, not_5_out, not_3_out, not_1_out);
  and and_36 (s5_5, FILA[2], FILA[0], COL[2], COL[0], not_7_out, not_5_out, not_3_out, not_1_out);
endmodule

module a4_Movimiento_LogicaEstados (
  input  ARR,
  input  IZQ,
  input  DER,
  input  ABJ,
  input  HIELO,
  input  PREMIO,
  input  POZO,
  input  FIN,
  output [3:0] COLUMNA,
  output [3:0] FILA,
  output [7:0] chex,
  output [7:0] cbin
);

  wire and_1_out, and_2_out, and_3_out, and_4_out, and_5_out, and_6_out, and_7_out, and_8_out, and_9_out,
       and_10_out, and_11_out, and_12_out, and_13_out, and_14_out, and_15_out, CLK, comparator_1_eq,
       comparator_2_eq, comparator_3_eq, comparator_4_eq, comparator_5_eq, counter_4_carry, counter_8_carry,
       not_1_out, not_2_out, not_3_out, not_4_out, not_5_out, not_6_out, not_7_out, not_8_out, not_9_out,
       not_10_out, not_11_out, not_12_out, or_1_out, or_2_out, or_3_out, or_4_out, or_5_out, or_6_out,
       or_7_out, or_8_out, or_9_out, or_10_out, or_11_out, or_12_out, Q;
  wire [1:0] counter_1_q, counter_2_q, counter_6_q, counter_7_q;
  wire [2:0] counter_3_q;
  wire [7:0] counter_5_q, multiplier_1_out;

  and and_1 (and_1_out, HIELO, DER);
  and and_2 (and_2_out, HIELO, IZQ);
  Counter #(.max('h2), .ongoal("stay"), .width(2)) counter_1 (
    .clr(or_1_out), .clk(and_3_out), .Q(counter_1_q));  // open: load, up, count, D, carry
  or or_1 (or_1_out, and_1_out, POZO, FIN, and_2_out);
  and and_3 (and_3_out, CLK, not_1_out);
  not not_1 (not_1_out, POZO);
  not not_2 (not_2_out, IZQ);
  or or_2 (or_2_out, DER, IZQ);
  or or_3 (or_3_out, and_2_out, POZO, FIN);
  and and_4 (and_4_out, CLK, not_3_out);
  not not_3 (not_3_out, POZO);
  Counter #(.max('h2), .ongoal("stay"), .width(2)) counter_2 (
    .clr(or_3_out), .clk(and_4_out), .Q(counter_2_q));  // open: load, up, count, D, carry
  not not_4 (not_4_out, comparator_1_eq);
  Comparator #(.width(2)) comparator_1 (.a(counter_1_q), .b(2'b10), .eq(comparator_1_eq));  // open: gt, lt
  and and_5 (and_5_out, CLK, not_4_out);
  D_Flip_Flop #(.trigger("high")) d_ff_1 (.D(FIN), .clk(FIN), .Q(Q), .reset(comparator_3_eq));  // open: Qn, preset
  not not_5 (not_5_out, Q);
  or or_4 (or_4_out, or_2_out, and_5_out);
  or or_5 (or_5_out, FIN, not_5_out, POZO);
  Counter #(.max('h4), .ongoal("stay"), .width(3)) counter_3 (
    .clr(or_5_out), .clk(and_6_out), .Q(counter_3_q));  // open: load, up, count, D, carry
  and and_6 (and_6_out, CLK, Q);
  Clock clock_1 (.out(CLK));
  Comparator #(.width(2)) comparator_2 (.a(counter_2_q), .b(2'b10), .eq(comparator_2_eq));  // open: gt, lt
  and and_7 (and_7_out, comparator_2_eq, not_2_out);
  or or_6 (or_6_out, POZO, FIN);
  Counter #(.max('h5), .ongoal("stay"), .width(4)) counter_4 (
    .clr(or_6_out), .up(and_7_out), .clk(or_4_out), .carry(counter_4_carry), .Q(COLUMNA));  // open: load, count, D
  Comparator #(.width(3)) comparator_3 (.a(3'b100), .b(counter_3_q), .eq(comparator_3_eq));  // open: gt, lt
  or or_7 (or_7_out, POZO, comparator_3_eq);
  Counter counter_5 (.clr(or_7_out), .clk(PREMIO), .Q(counter_5_q));  // open: load, up, count, D, carry
  Multiplier multiplier_1 (.a(counter_5_q), .b(8'h5), .out(multiplier_1_out));  // open: cin, cout
  Counter #(.max('h2), .ongoal("stay"), .width(2)) counter_6 (
    .clr(or_8_out), .clk(and_8_out), .Q(counter_6_q));  // open: load, up, count, D, carry
  or or_8 (or_8_out, and_9_out, POZO, FIN, and_10_out);
  and and_8 (and_8_out, CLK, not_6_out);
  not not_6 (not_6_out, POZO);
  and and_9 (and_9_out, HIELO, ABJ);
  and and_10 (and_10_out, HIELO, ARR);
  not not_7 (not_7_out, ARR);
  or or_9 (or_9_out, ABJ, ARR);
  Multiplexer #(.width(8)) multiplexer_1 (.in0(multiplier_1_out), .in1({8{1'b0}}), .out(cbin), .sel(and_11_out));
  and and_11 (and_11_out, not_8_out, and_12_out);
  not not_8 (not_8_out, Q);
  and and_12 (and_12_out, not_9_out, not_11_out);
  not not_9 (not_9_out, POZO);
  not not_10 (not_10_out, POZO);
  not not_11 (not_11_out, FIN);
  or or_10 (or_10_out, and_10_out, POZO, FIN);
  Counter #(.max('h2), .ongoal("stay"), .width(2)) counter_7 (
    .clr(or_10_out), .clk(and_13_out), .Q(counter_7_q));  // open: load, up, count, D, carry
  and and_13 (and_13_out, CLK, not_10_out);
  not not_12 (not_12_out, comparator_4_eq);
  Comparator #(.width(2)) comparator_4 (.a(counter_6_q), .b(2'b10), .eq(comparator_4_eq));  // open: gt, lt
  and and_14 (and_14_out, CLK, not_12_out);
  or or_11 (or_11_out, or_9_out, and_14_out);
  Comparator #(.width(2)) comparator_5 (.a(counter_7_q), .b(2'b10), .eq(comparator_5_eq));  // open: gt, lt
  and and_15 (and_15_out, comparator_5_eq, not_7_out);
  or or_12 (or_12_out, POZO, FIN);
  Counter #(.max('h5), .ongoal("stay"), .width(4)) counter_8 (
    .clr(or_12_out), .up(and_15_out), .clk(or_11_out), .carry(counter_8_carry), .Q(FILA));  // open: load, count, D

  assign chex = cbin;

  // Notes on the sheet:
  //   ===================== MOVIMIENTO IZQUIERDA Y DERECHA ====================
  //   ===================== LÓGICA DE PUNTAJE ====================
  //   ===================== MOVIMIENTO ARRIBA Y ABAJO ====================
endmodule

module a5_Tablero (
  input  GEN,
  input  ARR,
  input  IZQ,
  input  DER,
  input  ABJ,
  output [3:0] COL,
  output [3:0] FILA,
  output [7:0] chex,
  output [7:0] cbin,
  output POZO,
  output FIN,
  output l00,
  output l01,
  output l02,
  output l03,
  output l04,
  output l05,
  output l10,
  output l11,
  output l12,
  output l13,
  output l14,
  output l15,
  output l20,
  output l21,
  output l22,
  output l23,
  output l24,
  output l25,
  output l30,
  output l31,
  output l32,
  output l33,
  output l34,
  output l35,
  output l40,
  output l41,
  output l42,
  output l43,
  output l44,
  output l45,
  output l50,
  output l51,
  output l52,
  output l53,
  output l54,
  output l55
);

  wire casillero01_1_hielo, casillero01_1_pozo, casillero01_1_premio, casillero02_1_hielo,
       casillero02_1_pozo, casillero02_1_premio, casillero03_1_hielo, casillero03_1_pozo,
       casillero03_1_premio, casillero04_1_hielo, casillero04_1_pozo, casillero04_1_premio,
       casillero05_1_hielo, casillero05_1_pozo, casillero05_1_premio, casillero10_1_hielo,
       casillero10_1_pozo, casillero10_1_premio, casillero11_1_hielo, casillero11_1_pozo,
       casillero11_1_premio, casillero12_1_hielo, casillero12_1_pozo, casillero12_1_premio,
       casillero13_1_hielo, casillero13_1_pozo, casillero13_1_premio, casillero14_1_hielo,
       casillero14_1_pozo, casillero14_1_premio, casillero15_1_hielo, casillero15_1_pozo,
       casillero15_1_premio, casillero20_1_hielo, casillero20_1_pozo, casillero20_1_premio,
       casillero21_1_hielo, casillero21_1_pozo, casillero21_1_premio, casillero22_1_hielo,
       casillero22_1_pozo, casillero22_1_premio, casillero23_1_hielo, casillero23_1_pozo,
       casillero23_1_premio, casillero24_1_hielo, casillero24_1_pozo, casillero24_1_premio,
       casillero25_1_hielo, casillero25_1_pozo, casillero25_1_premio, casillero30_1_hielo,
       casillero30_1_pozo, casillero30_1_premio, casillero31_1_hielo, casillero31_1_pozo,
       casillero31_1_premio, casillero32_1_hielo, casillero32_1_pozo, casillero32_1_premio,
       casillero33_1_hielo, casillero33_1_pozo, casillero33_1_premio, casillero34_1_hielo,
       casillero34_1_pozo, casillero34_1_premio, casillero35_1_hielo, casillero35_1_pozo,
       casillero35_1_premio, casillero40_1_hielo, casillero40_1_pozo, casillero40_1_premio,
       casillero41_1_hielo, casillero41_1_pozo, casillero41_1_premio, casillero42_1_hielo,
       casillero42_1_pozo, casillero42_1_premio, casillero43_1_hielo, casillero43_1_pozo,
       casillero43_1_premio, casillero44_1_hielo, casillero44_1_pozo, casillero44_1_premio,
       casillero45_1_hielo, casillero45_1_pozo, casillero45_1_premio, casillero50_1_hielo,
       casillero50_1_pozo, casillero50_1_premio, casillero51_1_hielo, casillero51_1_pozo,
       casillero51_1_premio, casillero52_1_hielo, casillero52_1_pozo, casillero52_1_premio,
       casillero53_1_hielo, casillero53_1_pozo, casillero53_1_premio, casillero54_1_hielo,
       casillero54_1_pozo, casillero54_1_premio, casillero55_1_hielo, casillero55_1_pozo,
       casillero55_1_premio, CLK, HIELO_01, HIELO_02, HIELO_03, HIELO_04, HIELO_05, HIELO_10, HIELO_11,
       HIELO_12, HIELO_13, HIELO_14, HIELO_15, HIELO_20, HIELO_21, HIELO_22, HIELO_23, HIELO_24, HIELO_25,
       HIELO_30, HIELO_31, HIELO_32, HIELO_33, HIELO_34, HIELO_35, HIELO_40, HIELO_41, HIELO_42, HIELO_43,
       HIELO_44, HIELO_45, HIELO_50, HIELO_51, HIELO_52, HIELO_53, HIELO_54, HIELO_55, or_1_out, or_2_out,
       POZO_01, POZO_02, POZO_03, POZO_04, POZO_05, POZO_10, POZO_11, POZO_12, POZO_13, POZO_14, POZO_15,
       POZO_20, POZO_21, POZO_22, POZO_23, POZO_24, POZO_25, POZO_30, POZO_31, POZO_32, POZO_33, POZO_34,
       POZO_35, POZO_40, POZO_41, POZO_42, POZO_43, POZO_44, POZO_45, POZO_50, POZO_51, POZO_52, POZO_53,
       POZO_54, POZO_55, PREMIO_01, PREMIO_02, PREMIO_03, PREMIO_04, PREMIO_05, PREMIO_10, PREMIO_11,
       PREMIO_12, PREMIO_13, PREMIO_14, PREMIO_15, PREMIO_20, PREMIO_21, PREMIO_22, PREMIO_23, PREMIO_24,
       PREMIO_25, PREMIO_30, PREMIO_31, PREMIO_32, PREMIO_33, PREMIO_34, PREMIO_35, PREMIO_40, PREMIO_41,
       PREMIO_42, PREMIO_43, PREMIO_44, PREMIO_45, PREMIO_50, PREMIO_51, PREMIO_52, PREMIO_53, PREMIO_54,
       PREMIO_55;

  or or_1 (or_1_out, HIELO_01, HIELO_02, HIELO_03, HIELO_04, HIELO_05, HIELO_10, HIELO_11, HIELO_12, HIELO_13, HIELO_14, HIELO_15, HIELO_20, HIELO_21, HIELO_22, HIELO_23, HIELO_24, HIELO_25, HIELO_30, HIELO_31, HIELO_32, HIELO_33, HIELO_34, HIELO_35, HIELO_40, HIELO_41, HIELO_42, HIELO_43, HIELO_44, HIELO_45, HIELO_50, HIELO_51, HIELO_52, HIELO_53, HIELO_54, HIELO_55);
  a3_Posicion a3_posicion_1 (
    .FILA(FILA), .COL(COL), .s0_0(l00), .s0_1(l01), .s0_2(l02), .s0_3(l03), .s0_4(l04), .s0_5(l05),
    .s1_0(l10), .s1_1(l11), .s1_2(l12), .s1_3(l13), .s1_4(l14), .s1_5(l15), .s2_0(l20), .s2_1(l21),
    .s2_2(l22), .s2_3(l23), .s2_4(l24), .s2_5(l25), .s3_0(l30), .s3_1(l31), .s3_2(l32), .s3_3(l33),
    .s3_4(l34), .s3_5(l35), .s4_0(l40), .s4_1(l41), .s4_2(l42), .s4_3(l43), .s4_4(l44), .s4_5(l45),
    .s5_0(l50), .s5_1(l51), .s5_2(l52), .s5_3(l53), .s5_4(l54), .s5_5(l55));
  or or_2 (or_2_out, PREMIO_01, PREMIO_02, PREMIO_03, PREMIO_04, PREMIO_05, PREMIO_10, PREMIO_11, PREMIO_12, PREMIO_13, PREMIO_14, PREMIO_15, PREMIO_20, PREMIO_21, PREMIO_22, PREMIO_23, PREMIO_24, PREMIO_25, PREMIO_30, PREMIO_31, PREMIO_32, PREMIO_33, PREMIO_34, PREMIO_35, PREMIO_40, PREMIO_41, PREMIO_42, PREMIO_43, PREMIO_44, PREMIO_45, PREMIO_50, PREMIO_51, PREMIO_52, PREMIO_53, PREMIO_54, PREMIO_55);
  or or_3 (POZO, POZO_01, POZO_02, POZO_03, POZO_04, POZO_05, POZO_10, POZO_11, POZO_12, POZO_13, POZO_14, POZO_15, POZO_20, POZO_21, POZO_22, POZO_23, POZO_24, POZO_25, POZO_30, POZO_31, POZO_32, POZO_33, POZO_34, POZO_35, POZO_40, POZO_41, POZO_42, POZO_43, POZO_44, POZO_45, POZO_50, POZO_51, POZO_52, POZO_53, POZO_54, POZO_55);
  or or_4 (FIN, l55, l45, l35, l25, l15, l05);
  Clock clock_1 (.out(CLK));
  a4_Movimiento_LogicaEstados a4_movimiento_logicaestados_1 (
    .ARR(ARR), .IZQ(IZQ), .DER(DER), .ABJ(ABJ), .HIELO(or_1_out), .PREMIO(or_2_out), .POZO(POZO), .FIN(FIN),
    .COLUMNA(COL), .FILA(FILA), .chex(chex), .cbin(cbin));
  // casillero00 casillero00_1: pin names not known
  a2_Estado_Actual a2_estado_actual_1 (
    .PO(casillero10_1_pozo), .HIEL(casillero10_1_hielo), .PRE(casillero10_1_premio), .POS(l10),
    .POZO(POZO_10), .HIELO(HIELO_10), .PREMIO(PREMIO_10));
  casillero10 casillero10_1 (
    .GEN(GEN), .POZO(casillero10_1_pozo), .HIELO(casillero10_1_hielo), .PREMIO(casillero10_1_premio));  // open: GOMA
  a2_Estado_Actual a2_estado_actual_2 (
    .PO(casillero20_1_pozo), .HIEL(casillero20_1_hielo), .PRE(casillero20_1_premio), .POS(l20),
    .POZO(POZO_20), .HIELO(HIELO_20), .PREMIO(PREMIO_20));
  casillero20 casillero20_1 (
    .GEN(GEN), .POZO(casillero20_1_pozo), .HIELO(casillero20_1_hielo), .PREMIO(casillero20_1_premio));  // open: GOMA
  a2_Estado_Actual a2_estado_actual_3 (
    .PO(casillero30_1_pozo), .HIEL(casillero30_1_hielo), .PRE(casillero30_1_premio), .POS(l30),
    .POZO(POZO_30), .HIELO(HIELO_30), .PREMIO(PREMIO_30));
  a2_Estado_Actual a2_estado_actual_4 (
    .PO(casillero40_1_pozo), .HIEL(casillero40_1_hielo), .PRE(casillero40_1_premio), .POS(l40),
    .POZO(POZO_40), .HIELO(HIELO_40), .PREMIO(PREMIO_40));
  a2_Estado_Actual a2_estado_actual_5 (
    .PO(casillero50_1_pozo), .HIEL(casillero50_1_hielo), .PRE(casillero50_1_premio), .POS(l50),
    .POZO(POZO_50), .HIELO(HIELO_50), .PREMIO(PREMIO_50));
  casillero30 casillero30_1 (
    .GEN(GEN), .POZO(casillero30_1_pozo), .HIELO(casillero30_1_hielo), .PREMIO(casillero30_1_premio));  // open: GOMA
  casillero40 casillero40_1 (
    .GEN(GEN), .POZO(casillero40_1_pozo), .HIELO(casillero40_1_hielo), .PREMIO(casillero40_1_premio));  // open: GOMA
  casillero50 casillero50_1 (
    .GEN(GEN), .POZO(casillero50_1_pozo), .HIELO(casillero50_1_hielo), .PREMIO(casillero50_1_premio));  // open: GOMA
  a2_Estado_Actual a2_estado_actual_6 (
    .PO(casillero01_1_pozo), .HIEL(casillero01_1_hielo), .PRE(casillero01_1_premio), .POS(l01),
    .POZO(POZO_01), .HIELO(HIELO_01), .PREMIO(PREMIO_01));
  a2_Estado_Actual a2_estado_actual_7 (
    .PO(casillero11_1_pozo), .HIEL(casillero11_1_hielo), .PRE(casillero11_1_premio), .POS(l11),
    .POZO(POZO_11), .HIELO(HIELO_11), .PREMIO(PREMIO_11));
  a2_Estado_Actual a2_estado_actual_8 (
    .PO(casillero21_1_pozo), .HIEL(casillero21_1_hielo), .PRE(casillero21_1_premio), .POS(l21),
    .POZO(POZO_21), .HIELO(HIELO_21), .PREMIO(PREMIO_21));
  a2_Estado_Actual a2_estado_actual_9 (
    .PO(casillero31_1_pozo), .HIEL(casillero31_1_hielo), .PRE(casillero31_1_premio), .POS(l31),
    .POZO(POZO_31), .HIELO(HIELO_31), .PREMIO(PREMIO_31));
  casillero01 casillero01_1 (
    .GEN(GEN), .POZO(casillero01_1_pozo), .HIELO(casillero01_1_hielo), .PREMIO(casillero01_1_premio));  // open: GOMA
  casillero11 casillero11_1 (
    .GEN(GEN), .POZO(casillero11_1_pozo), .HIELO(casillero11_1_hielo), .PREMIO(casillero11_1_premio));  // open: GOMA
  casillero21 casillero21_1 (
    .GEN(GEN), .POZO(casillero21_1_pozo), .HIELO(casillero21_1_hielo), .PREMIO(casillero21_1_premio));  // open: GOMA
  casillero31 casillero31_1 (
    .GEN(GEN), .POZO(casillero31_1_pozo), .HIELO(casillero31_1_hielo), .PREMIO(casillero31_1_premio));  // open: GOMA
  a2_Estado_Actual a2_estado_actual_10 (
    .PO(casillero41_1_pozo), .HIEL(casillero41_1_hielo), .PRE(casillero41_1_premio), .POS(l41),
    .POZO(POZO_41), .HIELO(HIELO_41), .PREMIO(PREMIO_41));
  casillero41 casillero41_1 (
    .GEN(GEN), .POZO(casillero41_1_pozo), .HIELO(casillero41_1_hielo), .PREMIO(casillero41_1_premio));  // open: GOMA
  a2_Estado_Actual a2_estado_actual_11 (
    .PO(casillero51_1_pozo), .HIEL(casillero51_1_hielo), .PRE(casillero51_1_premio), .POS(l51),
    .POZO(POZO_51), .HIELO(HIELO_51), .PREMIO(PREMIO_51));
  casillero51 casillero51_1 (
    .GEN(GEN), .POZO(casillero51_1_pozo), .HIELO(casillero51_1_hielo), .PREMIO(casillero51_1_premio));  // open: GOMA
  a2_Estado_Actual a2_estado_actual_12 (
    .PO(casillero02_1_pozo), .HIEL(casillero02_1_hielo), .PRE(casillero02_1_premio), .POS(l02),
    .POZO(POZO_02), .HIELO(HIELO_02), .PREMIO(PREMIO_02));
  casillero02 casillero02_1 (
    .GEN(GEN), .POZO(casillero02_1_pozo), .HIELO(casillero02_1_hielo), .PREMIO(casillero02_1_premio));  // open: GOMA
  a2_Estado_Actual a2_estado_actual_13 (
    .PO(casillero12_1_pozo), .HIEL(casillero12_1_hielo), .PRE(casillero12_1_premio), .POS(l12),
    .POZO(POZO_12), .HIELO(HIELO_12), .PREMIO(PREMIO_12));
  casillero12 casillero12_1 (
    .GEN(GEN), .POZO(casillero12_1_pozo), .HIELO(casillero12_1_hielo), .PREMIO(casillero12_1_premio));  // open: GOMA
  a2_Estado_Actual a2_estado_actual_14 (
    .PO(casillero22_1_pozo), .HIEL(casillero22_1_hielo), .PRE(casillero22_1_premio), .POS(l22),
    .POZO(POZO_22), .HIELO(HIELO_22), .PREMIO(PREMIO_22));
  casillero22 casillero22_1 (
    .GEN(GEN), .POZO(casillero22_1_pozo), .HIELO(casillero22_1_hielo), .PREMIO(casillero22_1_premio));  // open: GOMA
  a2_Estado_Actual a2_estado_actual_15 (
    .PO(casillero32_1_pozo), .HIEL(casillero32_1_hielo), .PRE(casillero32_1_premio), .POS(l32),
    .POZO(POZO_32), .HIELO(HIELO_32), .PREMIO(PREMIO_32));
  casillero32 casillero32_1 (
    .GEN(GEN), .POZO(casillero32_1_pozo), .HIELO(casillero32_1_hielo), .PREMIO(casillero32_1_premio));  // open: GOMA
  a2_Estado_Actual a2_estado_actual_16 (
    .PO(casillero42_1_pozo), .HIEL(casillero42_1_hielo), .PRE(casillero42_1_premio), .POS(l42),
    .POZO(POZO_42), .HIELO(HIELO_42), .PREMIO(PREMIO_42));
  casillero42 casillero42_1 (
    .GEN(GEN), .POZO(casillero42_1_pozo), .HIELO(casillero42_1_hielo), .PREMIO(casillero42_1_premio));  // open: GOMA
  a2_Estado_Actual a2_estado_actual_17 (
    .PO(casillero52_1_pozo), .HIEL(casillero52_1_hielo), .PRE(casillero52_1_premio), .POS(l52),
    .POZO(POZO_52), .HIELO(HIELO_52), .PREMIO(PREMIO_52));
  casillero52 casillero52_1 (
    .GEN(GEN), .POZO(casillero52_1_pozo), .HIELO(casillero52_1_hielo), .PREMIO(casillero52_1_premio));  // open: GOMA
  a2_Estado_Actual a2_estado_actual_18 (
    .PO(casillero03_1_pozo), .HIEL(casillero03_1_hielo), .PRE(casillero03_1_premio), .POS(l03),
    .POZO(POZO_03), .HIELO(HIELO_03), .PREMIO(PREMIO_03));
  casillero03 casillero03_1 (
    .GEN(GEN), .POZO(casillero03_1_pozo), .HIELO(casillero03_1_hielo), .PREMIO(casillero03_1_premio));  // open: GOMA
  a2_Estado_Actual a2_estado_actual_19 (
    .PO(casillero13_1_pozo), .HIEL(casillero13_1_hielo), .PRE(casillero13_1_premio), .POS(l13),
    .POZO(POZO_13), .HIELO(HIELO_13), .PREMIO(PREMIO_13));
  casillero13 casillero13_1 (
    .GEN(GEN), .POZO(casillero13_1_pozo), .HIELO(casillero13_1_hielo), .PREMIO(casillero13_1_premio));  // open: GOMA
  a2_Estado_Actual a2_estado_actual_20 (
    .PO(casillero23_1_pozo), .HIEL(casillero23_1_hielo), .PRE(casillero23_1_premio), .POS(l23),
    .POZO(POZO_23), .HIELO(HIELO_23), .PREMIO(PREMIO_23));
  casillero23 casillero23_1 (
    .GEN(GEN), .POZO(casillero23_1_pozo), .HIELO(casillero23_1_hielo), .PREMIO(casillero23_1_premio));  // open: GOMA
  a2_Estado_Actual a2_estado_actual_21 (
    .PO(casillero33_1_pozo), .HIEL(casillero33_1_hielo), .PRE(casillero33_1_premio), .POS(l33),
    .POZO(POZO_33), .HIELO(HIELO_33), .PREMIO(PREMIO_33));
  casillero33 casillero33_1 (
    .GEN(GEN), .POZO(casillero33_1_pozo), .HIELO(casillero33_1_hielo), .PREMIO(casillero33_1_premio));  // open: GOMA
  a2_Estado_Actual a2_estado_actual_22 (
    .PO(casillero43_1_pozo), .HIEL(casillero43_1_hielo), .PRE(casillero43_1_premio), .POS(l43),
    .POZO(POZO_43), .HIELO(HIELO_43), .PREMIO(PREMIO_43));
  casillero43 casillero43_1 (
    .GEN(GEN), .POZO(casillero43_1_pozo), .HIELO(casillero43_1_hielo), .PREMIO(casillero43_1_premio));  // open: GOMA
  a2_Estado_Actual a2_estado_actual_23 (
    .PO(casillero53_1_pozo), .HIEL(casillero53_1_hielo), .PRE(casillero53_1_premio), .POS(l53),
    .POZO(POZO_53), .HIELO(HIELO_53), .PREMIO(PREMIO_53));
  casillero53 casillero53_1 (
    .GEN(GEN), .POZO(casillero53_1_pozo), .HIELO(casillero53_1_hielo), .PREMIO(casillero53_1_premio));  // open: GOMA
  a2_Estado_Actual a2_estado_actual_24 (
    .PO(casillero04_1_pozo), .HIEL(casillero04_1_hielo), .PRE(casillero04_1_premio), .POS(l04),
    .POZO(POZO_04), .HIELO(HIELO_04), .PREMIO(PREMIO_04));
  a2_Estado_Actual a2_estado_actual_25 (
    .PO(casillero14_1_pozo), .HIEL(casillero14_1_hielo), .PRE(casillero14_1_premio), .POS(l14),
    .POZO(POZO_14), .HIELO(HIELO_14), .PREMIO(PREMIO_14));
  a2_Estado_Actual a2_estado_actual_26 (
    .PO(casillero24_1_pozo), .HIEL(casillero24_1_hielo), .PRE(casillero24_1_premio), .POS(l24),
    .POZO(POZO_24), .HIELO(HIELO_24), .PREMIO(PREMIO_24));
  a2_Estado_Actual a2_estado_actual_27 (
    .PO(casillero34_1_pozo), .HIEL(casillero34_1_hielo), .PRE(casillero34_1_premio), .POS(l34),
    .POZO(POZO_34), .HIELO(HIELO_34), .PREMIO(PREMIO_34));
  a2_Estado_Actual a2_estado_actual_28 (
    .PO(casillero44_1_pozo), .HIEL(casillero44_1_hielo), .PRE(casillero44_1_premio), .POS(l44),
    .POZO(POZO_44), .HIELO(HIELO_44), .PREMIO(PREMIO_44));
  a2_Estado_Actual a2_estado_actual_29 (
    .PO(casillero54_1_pozo), .HIEL(casillero54_1_hielo), .PRE(casillero54_1_premio), .POS(l54),
    .POZO(POZO_54), .HIELO(HIELO_54), .PREMIO(PREMIO_54));
  casillero04 casillero04_1 (
    .GEN(GEN), .POZO(casillero04_1_pozo), .HIELO(casillero04_1_hielo), .PREMIO(casillero04_1_premio));  // open: GOMA
  casillero14 casillero14_1 (
    .GEN(GEN), .POZO(casillero14_1_pozo), .HIELO(casillero14_1_hielo), .PREMIO(casillero14_1_premio));  // open: GOMA
  casillero24 casillero24_1 (
    .GEN(GEN), .POZO(casillero24_1_pozo), .HIELO(casillero24_1_hielo), .PREMIO(casillero24_1_premio));  // open: GOMA
  casillero34 casillero34_1 (
    .GEN(GEN), .POZO(casillero34_1_pozo), .HIELO(casillero34_1_hielo), .PREMIO(casillero34_1_premio));  // open: GOMA
  casillero44 casillero44_1 (
    .GEN(GEN), .POZO(casillero44_1_pozo), .HIELO(casillero44_1_hielo), .PREMIO(casillero44_1_premio));  // open: GOMA
  casillero54 casillero54_1 (
    .GEN(GEN), .POZO(casillero54_1_pozo), .HIELO(casillero54_1_hielo), .PREMIO(casillero54_1_premio));  // open: GOMA
  a2_Estado_Actual a2_estado_actual_30 (
    .PO(casillero05_1_pozo), .HIEL(casillero05_1_hielo), .PRE(casillero05_1_premio), .POS(l05),
    .POZO(POZO_05), .HIELO(HIELO_05), .PREMIO(PREMIO_05));
  a2_Estado_Actual a2_estado_actual_31 (
    .PO(casillero15_1_pozo), .HIEL(casillero15_1_hielo), .PRE(casillero15_1_premio), .POS(l15),
    .POZO(POZO_15), .HIELO(HIELO_15), .PREMIO(PREMIO_15));
  a2_Estado_Actual a2_estado_actual_32 (
    .PO(casillero25_1_pozo), .HIEL(casillero25_1_hielo), .PRE(casillero25_1_premio), .POS(l25),
    .POZO(POZO_25), .HIELO(HIELO_25), .PREMIO(PREMIO_25));
  casillero05 casillero05_1 (
    .GEN(GEN), .POZO(casillero05_1_pozo), .HIELO(casillero05_1_hielo), .PREMIO(casillero05_1_premio));  // open: GOMA
  casillero15 casillero15_1 (
    .GEN(GEN), .POZO(casillero15_1_pozo), .HIELO(casillero15_1_hielo), .PREMIO(casillero15_1_premio));  // open: GOMA
  casillero25 casillero25_1 (
    .GEN(GEN), .POZO(casillero25_1_pozo), .HIELO(casillero25_1_hielo), .PREMIO(casillero25_1_premio));  // open: GOMA
  a2_Estado_Actual a2_estado_actual_33 (
    .PO(casillero35_1_pozo), .HIEL(casillero35_1_hielo), .PRE(casillero35_1_premio), .POS(l35),
    .POZO(POZO_35), .HIELO(HIELO_35), .PREMIO(PREMIO_35));
  casillero35 casillero35_1 (
    .GEN(GEN), .POZO(casillero35_1_pozo), .HIELO(casillero35_1_hielo), .PREMIO(casillero35_1_premio));  // open: GOMA
  a2_Estado_Actual a2_estado_actual_34 (
    .PO(casillero45_1_pozo), .HIEL(casillero45_1_hielo), .PRE(casillero45_1_premio), .POS(l45),
    .POZO(POZO_45), .HIELO(HIELO_45), .PREMIO(PREMIO_45));
  casillero45 casillero45_1 (
    .GEN(GEN), .POZO(casillero45_1_pozo), .HIELO(casillero45_1_hielo), .PREMIO(casillero45_1_premio));  // open: GOMA
  a2_Estado_Actual a2_estado_actual_35 (
    .PO(casillero55_1_pozo), .HIEL(casillero55_1_hielo), .PRE(casillero55_1_premio), .POS(l55),
    .POZO(POZO_55), .HIELO(HIELO_55), .PREMIO(PREMIO_55));
  casillero55 casillero55_1 (
    .GEN(GEN), .POZO(casillero55_1_pozo), .HIELO(casillero55_1_hielo), .PREMIO(casillero55_1_premio));  // open: GOMA
endmodule

module a6_Jugador_Jugando (
  input  POZO,
  input  FIN,
  output c44,
  output [3:0] PROX_PARTIDA_EN,
  output [3:0] JUGADOR
);

  wire and_1_out, and_2_out, and_3_out, and_4_out, and_5_out, and_6_out, CLK, not_1_out, not_2_out,
       not_3_out, not_4_out, not_5_out, not_6_out, not_7_out, not_8_out, or_1_out, or_2_out, or_3_out,
       or_4_out, Q;
  wire [3:0] counter_1_q, counter_2_q;

  Clock clock_1 (.out(CLK));
  D_Flip_Flop #(.trigger("high")) d_ff_1 (.D(or_1_out), .clk(or_1_out), .Q(Q), .reset(c44));  // open: Qn, preset
  or or_1 (or_1_out, FIN, POZO);
  not not_1 (not_1_out, Q);
  or or_2 (or_2_out, FIN, not_1_out, POZO);
  and and_1 (and_1_out, CLK, Q);
  Counter #(.max('hf), .ongoal("stay"), .width(4)) counter_1 (
    .clr(or_2_out), .clk(and_1_out), .Q(counter_1_q));  // open: load, up, count, D, carry
  Counter #(.max('h3), .width(4)) counter_2 (
    .clk(c44), .D(4'b0001), .Q(counter_2_q));  // open: clr, load, up, count, carry
  Comparator #(.width(4)) comparator_1 (.a(4'b0100), .b(counter_1_q), .eq(c44));  // open: gt, lt
  Adder #(.width(4)) adder_1 (.a(4'b0001), .b(counter_2_q), .out(JUGADOR));  // open: cin, cout
  or or_3 (or_3_out, FIN, POZO);
  and and_2 (and_2_out, Q, CLK);
  Counter #(.max('h4), .ongoal("stay"), .width(4)) counter_3 (
    .load(or_3_out), .up(1'b0), .clk(or_4_out), .D(4'b0100), .Q(PROX_PARTIDA_EN));  // open: clr, count, carry
  or or_4 (or_4_out, or_3_out, and_2_out);
  not not_2 (not_2_out, PROX_PARTIDA_EN[1]);
  and and_3 (and_3_out, PROX_PARTIDA_EN[0], not_2_out, not_3_out);
  not not_3 (not_3_out, PROX_PARTIDA_EN[2]);
  not not_4 (not_4_out, PROX_PARTIDA_EN[0]);
  and and_4 (and_4_out, not_4_out, PROX_PARTIDA_EN[1], not_5_out);
  not not_5 (not_5_out, PROX_PARTIDA_EN[2]);
  and and_5 (and_5_out, PROX_PARTIDA_EN[0], PROX_PARTIDA_EN[1], not_6_out);
  not not_6 (not_6_out, PROX_PARTIDA_EN[2]);
  not not_7 (not_7_out, PROX_PARTIDA_EN[0]);
  not not_8 (not_8_out, PROX_PARTIDA_EN[1]);
  and and_6 (and_6_out, not_7_out, not_8_out, PROX_PARTIDA_EN[2]);
  // Buzzer buzzer_1: pin names not known; wires that end beside it: and_6_out, 7'b0000101
  // Buzzer buzzer_2: pin names not known; wires that end beside it: and_5_out, 7'b0000101
  // Buzzer buzzer_3: pin names not known; wires that end beside it: and_4_out, 7'b0000101
  // Buzzer buzzer_4: pin names not known; wires that end beside it: 14'h352, and_3_out, 7'b0000101

  // Other names for the same wires on the sheet: C4 = c44
endmodule

module a7_Puntaje_Final (
  input  POZO,
  input  [7:0] cbin,
  output signo,
  output [3:0] u,
  output [3:0] c,
  output [3:0] d
);

  wire and_1_out, clock_1_out, comparator_1_eq, or_1_out;
  wire [2:0] counter_1_q;
  wire [3:0] binary_to_bcd_converter_1_p4;

  Clock clock_1 (.out(clock_1_out));
  or or_1 (or_1_out, POZO, comparator_1_eq);
  and and_1 (and_1_out, clock_1_out, signo);
  D_Flip_Flop d_ff_1 (.D(POZO), .clk(POZO), .Q(signo), .reset(comparator_1_eq));  // open: Qn, preset
  Counter #(.max('h4), .ongoal("stay"), .width(3)) counter_1 (
    .clr(or_1_out), .clk(and_1_out), .Q(counter_1_q));  // open: load, up, count, D, carry
  Comparator #(.width(3)) comparator_1 (.a(3'b100), .b(counter_1_q), .eq(comparator_1_eq));  // open: gt, lt
  // Binary_to_BCD_converter #(.binvalue(8)) binary_to_bcd_converter_1: pin names not known; wires that end beside it: cbin, c, d, binary_to_bcd_converter_1_p4
  Multiplexer #(.width(4)) multiplexer_1 (.in0(binary_to_bcd_converter_1_p4), .in1(4'b0001), .out(u), .sel(signo));

  // Other names for the same wires on the sheet: Q = signo
endmodule

module a8_Seleccionar_Partida (
  input  SP,
  output [3:0] P
);

  Counter #(.max('h7), .width(4)) counter_1 (.clk(SP), .Q(P));  // open: clr, load, up, count, D, carry
endmodule

module a9_Contador (
  input  POZO,
  input  FIN,
  output cx2
);

  wire and_1_out, CLK, not_1_out, or_1_out, or_2_out, Q;
  wire [1:0] counter_1_q;

  Clock clock_1 (.out(CLK));
  D_Flip_Flop #(.trigger("high")) d_ff_1 (.D(or_1_out), .clk(or_1_out), .Q(Q), .reset(cx2));  // open: Qn, preset
  or or_1 (or_1_out, FIN, POZO);
  not not_1 (not_1_out, Q);
  or or_2 (or_2_out, FIN, not_1_out, POZO);
  and and_1 (and_1_out, CLK, Q);
  Counter #(.max('h2), .ongoal("stay"), .width(2)) counter_1 (
    .clr(or_2_out), .clk(and_1_out), .Q(counter_1_q));  // open: load, up, count, D, carry
  Comparator #(.width(2)) comparator_1 (.a(2'b10), .b(counter_1_q), .eq(cx2));  // open: gt, lt

  // Other names for the same wires on the sheet: C2 = cx2
endmodule

module a10_Comprobar_Ganador_Historial (
  input  [7:0] P4,
  input  [7:0] P3,
  input  [7:0] P2,
  input  [7:0] P1,
  output JUG_1_GANADOR,
  output JUG_2_GANADOR,
  output JUG_3_GANADOR,
  output JUG_4_GANADOR,
  output EMPATE
);

  wire comparator_1_gt, comparator_2_gt, comparator_3_gt, comparator_4_gt, comparator_5_gt, comparator_6_gt,
       comparator_7_gt, comparator_8_gt, comparator_9_gt, comparator_10_gt, comparator_11_gt,
       comparator_12_gt, comparator_13_eq, comparator_14_eq, comparator_15_eq, comparator_16_eq, not_1_out,
       not_2_out, not_3_out, not_4_out, not_5_out, not_6_out, not_7_out, not_8_out;

  not not_1 (not_1_out, JUG_1_GANADOR);
  not not_2 (not_2_out, JUG_2_GANADOR);
  not not_3 (not_3_out, JUG_3_GANADOR);
  not not_4 (not_4_out, JUG_4_GANADOR);
  Comparator #(.mode("unsigned")) comparator_1 (.a(P1), .b(P2), .gt(comparator_1_gt));  // open: eq, lt
  Comparator #(.mode("unsigned")) comparator_2 (.a(P1), .b(P3), .gt(comparator_2_gt));  // open: eq, lt
  Comparator #(.mode("unsigned")) comparator_3 (.a(P1), .b(P4), .gt(comparator_3_gt));  // open: eq, lt
  Comparator #(.mode("unsigned")) comparator_4 (.a(P2), .b(P1), .gt(comparator_4_gt));  // open: eq, lt
  Comparator #(.mode("unsigned")) comparator_5 (.a(P2), .b(P3), .gt(comparator_5_gt));  // open: eq, lt
  Comparator #(.mode("unsigned")) comparator_6 (.a(P2), .b(P4), .gt(comparator_6_gt));  // open: eq, lt
  Comparator #(.mode("unsigned")) comparator_7 (.a(P3), .b(P1), .gt(comparator_7_gt));  // open: eq, lt
  Comparator #(.mode("unsigned")) comparator_8 (.a(P3), .b(P2), .gt(comparator_8_gt));  // open: eq, lt
  Comparator #(.mode("unsigned")) comparator_9 (.a(P3), .b(P4), .gt(comparator_9_gt));  // open: eq, lt
  Comparator #(.mode("unsigned")) comparator_10 (.a(P4), .b(P1), .gt(comparator_10_gt));  // open: eq, lt
  Comparator comparator_11 (.a(P4), .b(P2), .gt(comparator_11_gt));  // open: eq, lt
  Comparator #(.mode("unsigned")) comparator_12 (.a(P4), .b(P3), .gt(comparator_12_gt));  // open: eq, lt
  and and_1 (EMPATE, not_4_out, not_3_out, not_2_out, not_1_out);
  and and_2 (JUG_1_GANADOR, comparator_1_gt, comparator_2_gt, comparator_3_gt, not_5_out);
  and and_3 (JUG_2_GANADOR, comparator_4_gt, comparator_5_gt, comparator_6_gt, not_6_out);
  and and_4 (JUG_3_GANADOR, comparator_7_gt, comparator_8_gt, comparator_9_gt, not_7_out);
  and and_5 (JUG_4_GANADOR, comparator_10_gt, comparator_11_gt, comparator_12_gt, not_8_out);
  not not_5 (not_5_out, comparator_13_eq);
  Comparator comparator_13 (.a(P1), .b(8'h1), .eq(comparator_13_eq));  // open: gt, lt
  not not_6 (not_6_out, comparator_14_eq);
  Comparator comparator_14 (.a(P2), .b(8'h1), .eq(comparator_14_eq));  // open: gt, lt
  not not_7 (not_7_out, comparator_15_eq);
  Comparator comparator_15 (.a(P3), .b(8'h1), .eq(comparator_15_eq));  // open: gt, lt
  not not_8 (not_8_out, comparator_16_eq);
  Comparator comparator_16 (.a(P4), .b(8'h1), .eq(comparator_16_eq));  // open: gt, lt
endmodule

module casillero00 (
  output GOMA,
  output POZO,
  output HIELO,
  output PREMIO
);

  a1_Estado_Matriz a1_estado_matriz_1 (
    .in_1(1'b0), .in_2(1'b0), .GOMA(GOMA), .POZO(POZO), .HIELO(HIELO), .PREMIO(PREMIO));
endmodule

module casillero01 (
  input  GEN,
  output GOMA,
  output POZO,
  output HIELO,
  output PREMIO
);

  wire [1:0] random_1_out;

  Random #(.seed(111), .width(2)) random_1 (.next(GEN), .clk(GEN), .out(random_1_out));  // open: clr
  a1_Estado_Matriz a1_estado_matriz_1 (
    .in_1(random_1_out[0]), .in_2(random_1_out[1]), .GOMA(GOMA), .POZO(POZO), .HIELO(HIELO), .PREMIO(PREMIO));
endmodule

module casillero02 (
  input  GEN,
  output GOMA,
  output POZO,
  output HIELO,
  output PREMIO
);

  wire [1:0] random_1_out;

  Random #(.seed(222), .width(2)) random_1 (.next(GEN), .clk(GEN), .out(random_1_out));  // open: clr
  a1_Estado_Matriz a1_estado_matriz_1 (
    .in_1(random_1_out[0]), .in_2(random_1_out[1]), .GOMA(GOMA), .POZO(POZO), .HIELO(HIELO), .PREMIO(PREMIO));
endmodule

module casillero03 (
  input  GEN,
  output GOMA,
  output POZO,
  output HIELO,
  output PREMIO
);

  wire [1:0] random_1_out;

  Random #(.seed(380), .width(2)) random_1 (.next(GEN), .clk(GEN), .out(random_1_out));  // open: clr
  a1_Estado_Matriz a1_estado_matriz_1 (
    .in_1(random_1_out[0]), .in_2(random_1_out[1]), .GOMA(GOMA), .POZO(POZO), .HIELO(HIELO), .PREMIO(PREMIO));
endmodule

module casillero04 (
  input  GEN,
  output GOMA,
  output POZO,
  output HIELO,
  output PREMIO
);

  wire [1:0] random_1_out;

  Random #(.seed(480), .width(2)) random_1 (.next(GEN), .clk(GEN), .out(random_1_out));  // open: clr
  a1_Estado_Matriz a1_estado_matriz_1 (
    .in_1(random_1_out[0]), .in_2(random_1_out[1]), .GOMA(GOMA), .POZO(POZO), .HIELO(HIELO), .PREMIO(PREMIO));
endmodule

module casillero05 (
  input  GEN,
  output GOMA,
  output POZO,
  output HIELO,
  output PREMIO
);

  wire [1:0] random_1_out;

  Random #(.seed(577), .width(2)) random_1 (.next(GEN), .clk(GEN), .out(random_1_out));  // open: clr
  a1_Estado_Matriz a1_estado_matriz_1 (
    .in_1(random_1_out[0]), .in_2(random_1_out[1]), .GOMA(GOMA), .POZO(POZO), .HIELO(HIELO), .PREMIO(PREMIO));
endmodule

module casillero10 (
  input  GEN,
  output GOMA,
  output POZO,
  output HIELO,
  output PREMIO
);

  wire [1:0] random_1_out;

  Random #(.seed(1028), .width(2)) random_1 (.next(GEN), .clk(GEN), .out(random_1_out));  // open: clr
  a1_Estado_Matriz a1_estado_matriz_1 (
    .in_1(random_1_out[0]), .in_2(random_1_out[1]), .GOMA(GOMA), .POZO(POZO), .HIELO(HIELO), .PREMIO(PREMIO));
endmodule

module casillero11 (
  input  GEN,
  output GOMA,
  output POZO,
  output HIELO,
  output PREMIO
);

  wire [1:0] random_1_out;

  Random #(.seed(1155), .width(2)) random_1 (.next(GEN), .clk(GEN), .out(random_1_out));  // open: clr
  a1_Estado_Matriz a1_estado_matriz_1 (
    .in_1(random_1_out[0]), .in_2(random_1_out[1]), .GOMA(GOMA), .POZO(POZO), .HIELO(HIELO), .PREMIO(PREMIO));
endmodule

module casillero12 (
  input  GEN,
  output GOMA,
  output POZO,
  output HIELO,
  output PREMIO
);

  wire [1:0] random_1_out;

  Random #(.seed(1228), .width(2)) random_1 (.next(GEN), .clk(GEN), .out(random_1_out));  // open: clr
  a1_Estado_Matriz a1_estado_matriz_1 (
    .in_1(random_1_out[0]), .in_2(random_1_out[1]), .GOMA(GOMA), .POZO(POZO), .HIELO(HIELO), .PREMIO(PREMIO));
endmodule

module casillero13 (
  input  GEN,
  output GOMA,
  output POZO,
  output HIELO,
  output PREMIO
);

  wire [1:0] random_1_out;

  Random #(.seed(1323), .width(2)) random_1 (.next(GEN), .clk(GEN), .out(random_1_out));  // open: clr
  a1_Estado_Matriz a1_estado_matriz_1 (
    .in_1(random_1_out[0]), .in_2(random_1_out[1]), .GOMA(GOMA), .POZO(POZO), .HIELO(HIELO), .PREMIO(PREMIO));
endmodule

module casillero14 (
  input  GEN,
  output GOMA,
  output POZO,
  output HIELO,
  output PREMIO
);

  wire [1:0] random_1_out;

  Random #(.seed(1477), .width(2)) random_1 (.next(GEN), .clk(GEN), .out(random_1_out));  // open: clr
  a1_Estado_Matriz a1_estado_matriz_1 (
    .in_1(random_1_out[0]), .in_2(random_1_out[1]), .GOMA(GOMA), .POZO(POZO), .HIELO(HIELO), .PREMIO(PREMIO));
endmodule

module casillero15 (
  input  GEN,
  output GOMA,
  output POZO,
  output HIELO,
  output PREMIO
);

  wire [1:0] random_1_out;

  Random #(.seed(1569), .width(2)) random_1 (.next(GEN), .clk(GEN), .out(random_1_out));  // open: clr
  a1_Estado_Matriz a1_estado_matriz_1 (
    .in_1(random_1_out[0]), .in_2(random_1_out[1]), .GOMA(GOMA), .POZO(POZO), .HIELO(HIELO), .PREMIO(PREMIO));
endmodule

module casillero20 (
  input  GEN,
  output GOMA,
  output POZO,
  output HIELO,
  output PREMIO
);

  wire [1:0] random_1_out;

  Random #(.seed(2023), .width(2)) random_1 (.next(GEN), .clk(GEN), .out(random_1_out));  // open: clr
  a1_Estado_Matriz a1_estado_matriz_1 (
    .in_1(random_1_out[0]), .in_2(random_1_out[1]), .GOMA(GOMA), .POZO(POZO), .HIELO(HIELO), .PREMIO(PREMIO));
endmodule

module casillero21 (
  input  GEN,
  output GOMA,
  output POZO,
  output HIELO,
  output PREMIO
);

  wire [1:0] random_1_out;

  Random #(.seed(2119), .width(2)) random_1 (.next(GEN), .clk(GEN), .out(random_1_out));  // open: clr
  a1_Estado_Matriz a1_estado_matriz_1 (
    .in_1(random_1_out[0]), .in_2(random_1_out[1]), .GOMA(GOMA), .POZO(POZO), .HIELO(HIELO), .PREMIO(PREMIO));
endmodule

module casillero22 (
  input  GEN,
  output GOMA,
  output POZO,
  output HIELO,
  output PREMIO
);

  wire [1:0] random_1_out;

  Random #(.seed(2222), .width(2)) random_1 (.next(GEN), .clk(GEN), .out(random_1_out));  // open: clr
  a1_Estado_Matriz a1_estado_matriz_1 (
    .in_1(random_1_out[0]), .in_2(random_1_out[1]), .GOMA(GOMA), .POZO(POZO), .HIELO(HIELO), .PREMIO(PREMIO));
endmodule

module casillero23 (
  input  GEN,
  output GOMA,
  output POZO,
  output HIELO,
  output PREMIO
);

  wire [1:0] random_1_out;

  Random #(.seed(2359), .width(2)) random_1 (.next(GEN), .clk(GEN), .out(random_1_out));  // open: clr
  a1_Estado_Matriz a1_estado_matriz_1 (
    .in_1(random_1_out[0]), .in_2(random_1_out[1]), .GOMA(GOMA), .POZO(POZO), .HIELO(HIELO), .PREMIO(PREMIO));
endmodule

module casillero24 (
  input  GEN,
  output GOMA,
  output POZO,
  output HIELO,
  output PREMIO
);

  wire [1:0] random_1_out;

  Random #(.seed(2450), .width(2)) random_1 (.next(GEN), .clk(GEN), .out(random_1_out));  // open: clr
  a1_Estado_Matriz a1_estado_matriz_1 (
    .in_1(random_1_out[0]), .in_2(random_1_out[1]), .GOMA(GOMA), .POZO(POZO), .HIELO(HIELO), .PREMIO(PREMIO));
endmodule

module casillero25 (
  input  GEN,
  output GOMA,
  output POZO,
  output HIELO,
  output PREMIO
);

  wire [1:0] random_1_out;

  Random #(.seed(2568), .width(2)) random_1 (.next(GEN), .clk(GEN), .out(random_1_out));  // open: clr
  a1_Estado_Matriz a1_estado_matriz_1 (
    .in_1(random_1_out[0]), .in_2(random_1_out[1]), .GOMA(GOMA), .POZO(POZO), .HIELO(HIELO), .PREMIO(PREMIO));
endmodule

module casillero30 (
  input  GEN,
  output GOMA,
  output POZO,
  output HIELO,
  output PREMIO
);

  wire [1:0] random_1_out;

  Random #(.seed(3045), .width(2)) random_1 (.next(GEN), .clk(GEN), .out(random_1_out));  // open: clr
  a1_Estado_Matriz a1_estado_matriz_1 (
    .in_1(random_1_out[0]), .in_2(random_1_out[1]), .GOMA(GOMA), .POZO(POZO), .HIELO(HIELO), .PREMIO(PREMIO));
endmodule

module casillero31 (
  input  GEN,
  output GOMA,
  output POZO,
  output HIELO,
  output PREMIO
);

  wire [1:0] random_1_out;

  Random #(.seed(3127), .width(2)) random_1 (.next(GEN), .clk(GEN), .out(random_1_out));  // open: clr
  a1_Estado_Matriz a1_estado_matriz_1 (
    .in_1(random_1_out[0]), .in_2(random_1_out[1]), .GOMA(GOMA), .POZO(POZO), .HIELO(HIELO), .PREMIO(PREMIO));
endmodule

module casillero32 (
  input  GEN,
  output GOMA,
  output POZO,
  output HIELO,
  output PREMIO
);

  wire [1:0] random_1_out;

  Random #(.seed(3289), .width(2)) random_1 (.next(GEN), .clk(GEN), .out(random_1_out));  // open: clr
  a1_Estado_Matriz a1_estado_matriz_1 (
    .in_1(random_1_out[0]), .in_2(random_1_out[1]), .GOMA(GOMA), .POZO(POZO), .HIELO(HIELO), .PREMIO(PREMIO));
endmodule

module casillero33 (
  input  GEN,
  output GOMA,
  output POZO,
  output HIELO,
  output PREMIO
);

  wire [1:0] random_1_out;

  Random #(.seed(3345), .width(2)) random_1 (.next(GEN), .clk(GEN), .out(random_1_out));  // open: clr
  a1_Estado_Matriz a1_estado_matriz_1 (
    .in_1(random_1_out[0]), .in_2(random_1_out[1]), .GOMA(GOMA), .POZO(POZO), .HIELO(HIELO), .PREMIO(PREMIO));
endmodule

module casillero34 (
  input  GEN,
  output GOMA,
  output POZO,
  output HIELO,
  output PREMIO
);

  wire [1:0] random_1_out;

  Random #(.seed(3458), .width(2)) random_1 (.next(GEN), .clk(GEN), .out(random_1_out));  // open: clr
  a1_Estado_Matriz a1_estado_matriz_1 (
    .in_1(random_1_out[0]), .in_2(random_1_out[1]), .GOMA(GOMA), .POZO(POZO), .HIELO(HIELO), .PREMIO(PREMIO));
endmodule

module casillero35 (
  input  GEN,
  output GOMA,
  output POZO,
  output HIELO,
  output PREMIO
);

  wire [1:0] random_1_out;

  Random #(.seed(3566), .width(2)) random_1 (.next(GEN), .clk(GEN), .out(random_1_out));  // open: clr
  a1_Estado_Matriz a1_estado_matriz_1 (
    .in_1(random_1_out[0]), .in_2(random_1_out[1]), .GOMA(GOMA), .POZO(POZO), .HIELO(HIELO), .PREMIO(PREMIO));
endmodule

module casillero40 (
  input  GEN,
  output GOMA,
  output POZO,
  output HIELO,
  output PREMIO
);

  wire [1:0] random_1_out;

  Random #(.seed(4034), .width(2)) random_1 (.next(GEN), .clk(GEN), .out(random_1_out));  // open: clr
  a1_Estado_Matriz a1_estado_matriz_1 (
    .in_1(random_1_out[0]), .in_2(random_1_out[1]), .GOMA(GOMA), .POZO(POZO), .HIELO(HIELO), .PREMIO(PREMIO));
endmodule

module casillero41 (
  input  GEN,
  output GOMA,
  output POZO,
  output HIELO,
  output PREMIO
);

  wire [1:0] random_1_out;

  Random #(.seed(4120), .width(2)) random_1 (.next(GEN), .clk(GEN), .out(random_1_out));  // open: clr
  a1_Estado_Matriz a1_estado_matriz_1 (
    .in_1(random_1_out[0]), .in_2(random_1_out[1]), .GOMA(GOMA), .POZO(POZO), .HIELO(HIELO), .PREMIO(PREMIO));
endmodule

module casillero42 (
  input  GEN,
  output GOMA,
  output POZO,
  output HIELO,
  output PREMIO
);

  wire [1:0] random_1_out;

  Random #(.seed(4270), .width(2)) random_1 (.next(GEN), .clk(GEN), .out(random_1_out));  // open: clr
  a1_Estado_Matriz a1_estado_matriz_1 (
    .in_1(random_1_out[0]), .in_2(random_1_out[1]), .GOMA(GOMA), .POZO(POZO), .HIELO(HIELO), .PREMIO(PREMIO));
endmodule

module casillero43 (
  input  GEN,
  output GOMA,
  output POZO,
  output HIELO,
  output PREMIO
);

  wire [1:0] random_1_out;

  Random #(.seed(4330), .width(2)) random_1 (.next(GEN), .clk(GEN), .out(random_1_out));  // open: clr
  a1_Estado_Matriz a1_estado_matriz_1 (
    .in_1(random_1_out[0]), .in_2(random_1_out[1]), .GOMA(GOMA), .POZO(POZO), .HIELO(HIELO), .PREMIO(PREMIO));
endmodule

module casillero44 (
  input  GEN,
  output GOMA,
  output POZO,
  output HIELO,
  output PREMIO
);

  wire [1:0] random_1_out;

  Random #(.seed(4479), .width(2)) random_1 (.next(GEN), .clk(GEN), .out(random_1_out));  // open: clr
  a1_Estado_Matriz a1_estado_matriz_1 (
    .in_1(random_1_out[0]), .in_2(random_1_out[1]), .GOMA(GOMA), .POZO(POZO), .HIELO(HIELO), .PREMIO(PREMIO));
endmodule

module casillero45 (
  input  GEN,
  output GOMA,
  output POZO,
  output HIELO,
  output PREMIO
);

  wire [1:0] random_1_out;

  Random #(.seed(4559), .width(2)) random_1 (.next(GEN), .clk(GEN), .out(random_1_out));  // open: clr
  a1_Estado_Matriz a1_estado_matriz_1 (
    .in_1(random_1_out[0]), .in_2(random_1_out[1]), .GOMA(GOMA), .POZO(POZO), .HIELO(HIELO), .PREMIO(PREMIO));
endmodule

module casillero50 (
  input  GEN,
  output GOMA,
  output POZO,
  output HIELO,
  output PREMIO
);

  wire [1:0] random_1_out;

  Random #(.seed(5025), .width(2)) random_1 (.next(GEN), .clk(GEN), .out(random_1_out));  // open: clr
  a1_Estado_Matriz a1_estado_matriz_1 (
    .in_1(random_1_out[0]), .in_2(random_1_out[1]), .GOMA(GOMA), .POZO(POZO), .HIELO(HIELO), .PREMIO(PREMIO));
endmodule

module casillero51 (
  input  GEN,
  output GOMA,
  output POZO,
  output HIELO,
  output PREMIO
);

  wire [1:0] random_1_out;

  Random #(.seed(5150), .width(2)) random_1 (.next(GEN), .clk(GEN), .out(random_1_out));  // open: clr
  a1_Estado_Matriz a1_estado_matriz_1 (
    .in_1(random_1_out[0]), .in_2(random_1_out[1]), .GOMA(GOMA), .POZO(POZO), .HIELO(HIELO), .PREMIO(PREMIO));
endmodule

module casillero52 (
  input  GEN,
  output GOMA,
  output POZO,
  output HIELO,
  output PREMIO
);

  wire [1:0] random_1_out;

  Random #(.seed(5279), .width(2)) random_1 (.next(GEN), .clk(GEN), .out(random_1_out));  // open: clr
  a1_Estado_Matriz a1_estado_matriz_1 (
    .in_1(random_1_out[0]), .in_2(random_1_out[1]), .GOMA(GOMA), .POZO(POZO), .HIELO(HIELO), .PREMIO(PREMIO));
endmodule

module casillero53 (
  input  GEN,
  output GOMA,
  output POZO,
  output HIELO,
  output PREMIO
);

  wire [1:0] random_1_out;

  Random #(.seed(5322), .width(2)) random_1 (.next(GEN), .clk(GEN), .out(random_1_out));  // open: clr
  a1_Estado_Matriz a1_estado_matriz_1 (
    .in_1(random_1_out[0]), .in_2(random_1_out[1]), .GOMA(GOMA), .POZO(POZO), .HIELO(HIELO), .PREMIO(PREMIO));
endmodule

module casillero54 (
  input  GEN,
  output GOMA,
  output POZO,
  output HIELO,
  output PREMIO
);

  wire [1:0] random_1_out;

  Random #(.seed(5434), .width(2)) random_1 (.next(GEN), .clk(GEN), .out(random_1_out));  // open: clr
  a1_Estado_Matriz a1_estado_matriz_1 (
    .in_1(random_1_out[0]), .in_2(random_1_out[1]), .GOMA(GOMA), .POZO(POZO), .HIELO(HIELO), .PREMIO(PREMIO));
endmodule

module casillero55 (
  input  GEN,
  output GOMA,
  output POZO,
  output HIELO,
  output PREMIO
);

  wire [1:0] random_1_out;

  Random #(.seed(5557), .width(2)) random_1 (.next(GEN), .clk(GEN), .out(random_1_out));  // open: clr
  a1_Estado_Matriz a1_estado_matriz_1 (
    .in_1(random_1_out[0]), .in_2(random_1_out[1]), .GOMA(GOMA), .POZO(POZO), .HIELO(HIELO), .PREMIO(PREMIO));
endmodule
